# Fritzing sketch smartgreenhousesensors (saved by Fritzing 0.9.3b)
breadboards: 1

parts:
  Raspberry_Pi_1 = Raspberry Pi 3 [part_number=RPI-3-V1.2]
  DHT1 = DHT22 Humidity and Temperature Sensor
  Part1 = Adafruit VEML6075 UV Sensor Breakout [part_number=3964]
  R1 = Resistor [tolerance=±5% resistance=10k package=THT]
  Part2 = Adafruit STEMMA Soil Sensor - I2C Capacitive Moisture Sensor [part_number="Adafruit #4026"]
  Part3 = Adafruit SGP30 Gas Sensor
  hc-sr1 = hc-sr04
  R2 = Resistor [tolerance=±5% resistance=330 package=THT]
  R3 = Resistor [tolerance=±5% resistance=470 package=THT]

nets:
  VIN: Raspberry_Pi_1.3v3, DHT1.VDD, Part1.VIN, R1.Pin_0, Part2.VIN, Part3.VIN, hc-sr1.VCC
  N1: Raspberry_Pi_1.GPIO2, Part1.SDA
  N2: Raspberry_Pi_1.GPIO3, Part1.SCL
  N3: Raspberry_Pi_1.GIPO17, Part2.SCL
  N4: Raspberry_Pi_1.GIPO27, Part2.SDA
  N5: Raspberry_Pi_1.GIPO10, Part3.SCL
  N6: Raspberry_Pi_1.GIPO9, Part3.SDA
  N7: Raspberry_Pi_1.GIPO7, R2.Pin_1, R3.Pin_1
  N8: Raspberry_Pi_1.GIPO8, hc-sr1.Trig
  N9: Raspberry_Pi_1.GIPO14, DHT1.DATA, R1.Pin_1
  GND: Raspberry_Pi_1.GND, DHT1.GND, Part1.GND, Part2.GND, Part3.GND, hc-sr1.GND, R3.Pin_0
  N10: hc-sr1.Echo, R2.Pin_0

notes:
  DHT22 Temperature & Humidity Sensor
  VEML6075 UVA & UVB Light Sensor
  STEMMA Soil & I2C Capacitive Moisture Sensor
  SGP30 Air Quality Sensor
  HC-SR04
  Distance Sensor

custom parts:
  Adafruit VEML6075 UV Sensor Breakout: This little sensor is a great way to add UVA and UVB light sensing to any microcontroller project. The VEML6075 from Vishay has both true UVA and UVB band light sensors and an I2C-controlled ADC that will take readings and integrate them. The sensor also comes with calibration registers so you can easily convert the UVA/UVB readings into the UV Index. Compared to our other UV sensors, this one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
  Adafruit STEMMA Soil Sensor - I2C Capacitive Moisture Sensor: Most low cost soil sensors are resistive style, where there's two prongs and the sensor measures the conductivity between the two. These work OK at first, but eventually start to oxidize because of the exposed metal. Even if they're gold plated! The resistivity measurement goes up and up, so you constantly have to re-calibrate your code. Also, resistive measurements don't always work in loose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
